# Fritzing sketch rhtlogger (saved by Fritzing 0.9.2b)

parts:
  LCM1602_IIC1 = LCM1602 IIC [part_number="LCM1602 IIC" chip_label="LCM1602 IIC" package="DIP (Dual Inline) [THT]"]
  LCD1 = LCD screen
  Part1 = Arduino Uno (Rev3)
  Part2 = Memoire 1.0 - SD card log shield
  S1 = Pushbutton [package="[THT]"]
  R2 = Resistor [tolerance=±5% resistance=10k package=THT]
  Part3 = Humidity Temperature Sensor SHT15

nets:
  VSS: LCM1602_IIC1.VSS, LCD1.VSS
  VDD: LCM1602_IIC1.VDD, LCD1.VDD
  N1: LCM1602_IIC1.V0, LCD1.V0
  N2: LCM1602_IIC1.RS, LCD1.RS
  N3: LCM1602_IIC1.RW, LCD1.R/W
  N4: LCM1602_IIC1.E, LCD1.E
  N5: LCM1602_IIC1.D0, LCD1.DB0
  N6: LCM1602_IIC1.D1, LCD1.DB1
  N7: LCM1602_IIC1.D2, LCD1.DB2
  N8: LCM1602_IIC1.D3, LCD1.DB3
  N9: LCM1602_IIC1.D4, LCD1.DB4
  N10: LCM1602_IIC1.D5, LCD1.DB5
  N11: LCM1602_IIC1.D6, LCD1.DB6
  N12: LCM1602_IIC1.D7, LCD1.DB7
  N13: LCM1602_IIC1.A, LCD1.LED+
  N14: LCM1602_IIC1.K, LCD1.LED-
  GND: LCM1602_IIC1.GND, Part1.GND, Part2.GND, R2.Pin_0, Part3.GND
  VCC: LCM1602_IIC1.VCC, Part1.5V, Part2.DIG_8, Part2.+5V, S1.Pin_3, S1.Pin_4
  N15: LCM1602_IIC1.SDA, Part1.A4/SDA, Part3.SDA
  N16: LCM1602_IIC1.SCL, Part1.A5/SCL, Part3.SCL
  N17: Part1.D10_PWM/SS, Part2.DIG_10
  N18: Part1.D11_PWM/MOSI, Part2.DIG_11
  N19: Part1.D12/MISO, Part2.DIG_12
  N20: Part1.D13/SCK, Part2.DIG_13
  3V3: Part2.3V3, Part3.VCC
  N21: S1.Pin_1, S1.Pin_2, R2.Pin_1

custom parts:
  LCM1602 IIC: I2C-Module to use a 1602 or 2004 LCD on with the wire.h libory Serial LCD Modul
  Humidity Temperature Sensor SHT15: Description: This is a simple breakout board for the SHT15 humidity sensor from Sensirion. The SHT15 digital humidity and temperature sensor is fully calibrated and offers high precision and excellent long-term stability at low cost. The digital CMOSens Technology integrates two sensors and readout circuitry on one single chip. These sensors are really impressive! Very sensitive and straight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
