# Fritzing sketch rhtlogger_promini (saved by Fritzing 0.9.2b)
breadboards: 1

parts:
  LCM1602_IIC1 = LCM1602 IIC [part_number="LCM1602 IIC" chip_label="LCM1602 IIC" package="DIP (Dual Inline) [THT]"]
  LCD1 = LCD screen
  S1 = Pushbutton [package="[THT]"]
  R2 = Resistor [tolerance=±5% resistance=10k package=THT]
  Part3 = Humidity Temperature Sensor SHT15
  Part4 = MicroSD Card Module
  Part5 = Arduino Pro Mini v13
  JACK1 = 2.1mm Barrel Jack with Terminal Block
  RTC1 = DS1307 RTC Breakout
  IC1 = Voltage Regulator AMS1117 [package=sot223]

nets:
  VSS: LCM1602_IIC1.VSS, LCD1.VSS
  VDD: LCM1602_IIC1.VDD, LCD1.VDD
  N1: LCM1602_IIC1.V0, LCD1.V0
  N2: LCM1602_IIC1.RS, LCD1.RS
  N3: LCM1602_IIC1.RW, LCD1.R/W
  N4: LCM1602_IIC1.E, LCD1.E
  N5: LCM1602_IIC1.D0, LCD1.DB0
  N6: LCM1602_IIC1.D1, LCD1.DB1
  N7: LCM1602_IIC1.D2, LCD1.DB2
  N8: LCM1602_IIC1.D3, LCD1.DB3
  N9: LCM1602_IIC1.D4, LCD1.DB4
  N10: LCM1602_IIC1.D5, LCD1.DB5
  N11: LCM1602_IIC1.D6, LCD1.DB6
  N12: LCM1602_IIC1.D7, LCD1.DB7
  N13: LCM1602_IIC1.A, LCD1.LED+
  N14: LCM1602_IIC1.K, LCD1.LED-
  GND: LCM1602_IIC1.GND, R2.Pin_0, Part3.GND, Part4.GND, Part5.GND, JACK1.NEG, RTC1.GND, IC1.GND
  VCC: LCM1602_IIC1.VCC, S1.Pin_3, S1.Pin_4, Part4.VCC, Part5.VCC, Part5.D8, JACK1.POS, RTC1.5V, IC1.IN
  N15: LCM1602_IIC1.SDA, Part3.SDA, Part5.A4, RTC1.SDA
  N16: LCM1602_IIC1.SCL, Part3.SCL, Part5.A5, RTC1.SCL
  N17: S1.Pin_1, S1.Pin_2, R2.Pin_1
  N18: Part3.VCC, IC1.OUT
  N19: Part4.MISO, Part5.D12/MISO
  N20: Part4.MOSI, Part5.D11_PWM/MOSI
  N21: Part4.SCK, Part5.D13/SCK
  N22: Part4.CS, Part5.D10_PWM/SS

custom parts:
  LCM1602 IIC: I2C-Module to use a 1602 or 2004 LCD on with the wire.h libory Serial LCD Modul
  Humidity Temperature Sensor SHT15: Description: This is a simple breakout board for the SHT15 humidity sensor from Sensirion. The SHT15 digital humidity and temperature sensor is fully calibrated and offers high precision and excellent long-term stability at low cost. The digital CMOSens Technology integrates two sensors and readout circuitry on one single chip. These sensors are really impressive! Very sensitive and straight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
  DS1307 RTC Breakout: DS1307 Real-time Clock Breakout Board with Battery
